# Fritzing sketch SunneeD_Circuit (saved by Fritzing 0.9.6b)
breadboards: 1

parts:
  MCU1 = Raspberry Pi Zero
  Part1 = EasyDriver_v44
  Part2 = sparkfun-battery-babysitter
  U1 = LIPO-1000mAh [package=lipo-1000]
  M1 = Stepper Motor - Bipolar  # not connected

nets:
  N1: MCU1.pin_1, MCU1.pin_17, Part2.OUT, Part2.V_PU
  N2: MCU1.pin_2, Part1.V+
  N3: MCU1.pin_3, Part2.SDA
  N4: MCU1.pin_5, Part2.SCL
  GND: MCU1.pin_6, MCU1.pin_9, MCU1.pin_20, Part1.GND, Part2.GND, U1.-
  N5: MCU1.pin_16, Part1.OUT1B
  N6: MCU1.pin_18, Part1.OUT1A
  N7: MCU1.pin_19, Part1.OUT2B
  N8: MCU1.pin_22, Part1.OUT2A
  N9: Part2.BATTERY_IN, U1.+
