# Fritzing sketch SunneeD_Wiring_v1 (saved by Fritzing 0.9.6b)
breadboards: 1

parts:
  MCU1 = Raspberry Pi Zero
  Part1 = EasyDriver_v44
  Part2 = sparkfun-battery-babysitter
  U1 = LIPO-1000mAh [package=lipo-1000]  # not connected
  M1 = Stepper Motor - Bipolar  # not connected

nets:
  N1: MCU1.pin_1, Part2.OUT
  N2: MCU1.pin_2, Part1.V+
  GND: MCU1.pin_6, MCU1.pin_9, Part1.GND, Part2.GND
  N3: MCU1.pin_16, Part1.OUT1B
  N4: MCU1.pin_18, Part1.OUT1A
  N5: MCU1.pin_19, Part1.OUT2B
  N6: MCU1.pin_22, Part1.OUT2A
